// Logisim project cpu.circ as structural Verilog: 1 circuit, main circuit cpu
module cpu (
  input  clk,
  input  [31:0] Instruction,
  input  [31:0] MemReadData,
  output [31:0] MemAddress,
  output [31:0] ProgramCounter,
  output [31:0] ra,
  output [31:0] sp,
  output [31:0] t0,
  output [31:0] t1,
  output [31:0] t2,
  output [31:0] s0,
  output [31:0] s1,
  output [31:0] a0,
  output [3:0] MemWriteMask,
  output [31:0] MemWriteData
);

  wire branch_comp_1_breq, branch_comp_1_brlt, BrUn, BSel, RegWEn;
  wire [2:0] ImmSel;
  wire [3:0] control_logic_1_alusel;
  wire [31:0] adder_1_out, alu_1_aluresult, imm_gen_1_immediate, multiplexer_1_out, regfile_1_readdata1,
       regfile_1_readdata2;

  Register #(.width(32)) PC (.D(adder_1_out), .clk(clk), .Q(ProgramCounter));  // open: en, clr
  Adder #(.width(32)) adder_1 (.a(ProgramCounter), .b(32'h4), .out(adder_1_out));  // open: cin, cout
  regfile regfile_1 (
    .ReadIndex1(Instruction[19:15]), .ReadIndex2(Instruction[24:20]), .WriteIndex(Instruction[11:7]),
    .WriteData(alu_1_aluresult), .RegWEn(RegWEn), .clk(clk), .ra(ra), .sp(sp), .t0(t0), .t1(t1), .t2(t2),
    .s0(s0), .s1(s1), .a0(a0), .ReadData1(regfile_1_readdata1), .ReadData2(regfile_1_readdata2));
  imm_gen imm_gen_1 (.Instruction(Instruction), .ImmSel(ImmSel), .Immediate(imm_gen_1_immediate));
  Multiplexer #(.width(32)) multiplexer_1 (
    .in0(regfile_1_readdata2), .in1(imm_gen_1_immediate), .out(multiplexer_1_out), .sel(BSel));
  control_logic control_logic_1 (
    .Instruction(Instruction), .BrEq(branch_comp_1_breq), .BrLt(branch_comp_1_brlt), .RegWEn(RegWEn),
    .ImmSel(ImmSel), .BrUn(BrUn), .BSel(BSel), .ALUSel(control_logic_1_alusel));  // open: PCSel, ASel, MemWEn, WBSel
  alu alu_1 (
    .A(regfile_1_readdata1), .B(multiplexer_1_out), .ALUSel(control_logic_1_alusel),
    .ALUResult(alu_1_aluresult));
  branch_comp branch_comp_1 (
    .BrData1(regfile_1_readdata1), .BrData2(multiplexer_1_out), .BrUn(BrUn), .BrEq(branch_comp_1_breq),
    .BrLt(branch_comp_1_brlt));
  // partial_store partial_store_1: pin names not known
  // partial_load partial_load_1: pin names not known

  // Other names for the same wires on the sheet: rd[4:0] = Instruction[11:7]; rs1[4:0] = Instruction[19:15];
  //   rs2[4:0] = Instruction[24:20]

  // Notes on the sheet:
  //   To IMEM
  //   IMEM (do **NOT** move this)
  //   From IMEM
  //   Inputs/Outputs for testing. Do **NOT** move these.
  //   To DMEM
  //   DMEM (do **NOT** move this)
  //   From DMEM
endmodule
